# Fritzing sketch Speedo Min (saved by Fritzing 1.0.2b)
circuit board: 11cm x 5.8cm
breadboards: 2

parts:
  GPS = GT-U7 NEO6M GPS
  J4 = female pin header, 2 pins [form="♀ (female)"]
  I2C_Multiplexer = Adafruit TCA9548A
  Motor_Controller = Adafruit TB6612 DC and Stepper Motor Driver [part_number="Adafruit #2448"]
  J1 = female pin header, 2 pins [form="♀ (female)"]
  J5 = female pin header, 2 pins [form="♀ (female)"]
  J7 = female pin header, 2 pins [form="♀ (female)"]
  J2 = female pin header, 2 pins [form="♀ (female)"]
  J6 = female pin header, 2 pins [form="♀ (female)"]
  J8 = female pin header, 2 pins [form="♀ (female)"]
  J3 = female pin header, 2 pins [form="♀ (female)"]
  D1 = TVS Diode [part_number=P6KE20A package="300 mil [THT]"]
  Real-time_Clock = Adafruit DS3231 [part_number="Adafruit #3013"]
  FRAM = SPI Non-Volatile FRAM 8KB [mpn="Adafruit #1897"]
  C1 = Ceramic Capacitor [capacitance=100nF voltage=35V package="200 mil [THT, multilayer]"]
  Level_Shifter = TXB0104 4-channel Bi-Directional Level Shifter
  Arduino_Nano_Every = Arduino Nano Every

nets:
  N1: GPS.Pin_2, Level_Shifter.A1
  N2: GPS.Pin_3, Level_Shifter.A2
  GND: GPS.Pin_4, J4.pin2, I2C_Multiplexer.GND, I2C_Multiplexer.A0, I2C_Multiplexer.A1, I2C_Multiplexer.A2, Motor_Controller.GND, J1.pin2, J5.pin1, J7.pin1, D1.anode, Real-time_Clock.GND, FRAM.GND, C1.0, Level_Shifter.GND, Arduino_Nano_Every.GND
  N3: GPS.Pin_5, Level_Shifter.LV, Arduino_Nano_Every.3V3
  N4: J4.pin1, Arduino_Nano_Every.D7
  N5: I2C_Multiplexer.3SDA, Real-time_Clock.SDA
  N6: I2C_Multiplexer.3SCL, Real-time_Clock.SCL
  N7: I2C_Multiplexer.5SDA, J6.pin1
  N8: I2C_Multiplexer.5SCL, J6.pin2
  N9: I2C_Multiplexer.6SDA, J8.pin1
  N10: I2C_Multiplexer.6SCL, J8.pin2
  VCC: I2C_Multiplexer.VCC, Motor_Controller.Vmotor, Motor_Controller.PWRIN, Motor_Controller.VCC, Motor_Controller.PWMB, Motor_Controller.PWMA, J5.pin2, J7.pin2, Real-time_Clock.Vin, FRAM.MOSI, FRAM.VCC, Level_Shifter.HV, Arduino_Nano_Every.D11/MOSI, Arduino_Nano_Every.+5V
  N11: I2C_Multiplexer.INPUTSDA, Arduino_Nano_Every.A4
  N12: I2C_Multiplexer.INPUTSCL, Arduino_Nano_Every.A5
  N13: Motor_Controller.BIN2, Arduino_Nano_Every.D9~
  N14: Motor_Controller.BIN1, Arduino_Nano_Every.D8
  N15: Motor_Controller.AIN1, Arduino_Nano_Every.D5~
  N16: Motor_Controller.AIN2, Arduino_Nano_Every.D4
  N17: Motor_Controller.MOTORA1, J3.pin2
  N18: Motor_Controller.MOTORA2, J3.pin1
  N19: Motor_Controller.MOTORB2, J2.pin2
  N20: Motor_Controller.MOTORB1, J2.pin1
  N21: J1.pin1, D1.cathode, C1.1, Arduino_Nano_Every.VIN
  N22: FRAM.CS, Arduino_Nano_Every.D10~
  N23: FRAM.MISO, Arduino_Nano_Every.D12~/MISO
  N24: FRAM.SCK, Arduino_Nano_Every.D13~
  N25: Level_Shifter.B1, Arduino_Nano_Every.RX
  N26: Level_Shifter.B2, Arduino_Nano_Every.TX
  N27: Arduino_Nano_Every.RESET, Arduino_Nano_Every.A7

notes:
  Trip Odometer
  Odometer
  Guage Motor
  Trip
  Switch
  SDA
  SCL
  VCC
  GND
  D3
  TR
  BR
  TL
  BL
  From 12V
  12V
  From
  Battery
  To Speedomter
  Stepper Motor
  To OLED
  Display
  (Odometer)
  {Trip Odometer}
  Reset
  Serial
  Interface
  Ignition Switch
  FRAM
  RTC

custom parts:
  GT-U7 NEO6M GPS: GT-U7 NEO6M GPS.
  Adafruit TCA9548A: You just found the perfect I2C sensor, and you want to wire up two or three or more of them to your Arduino when you realize "Uh oh, this chip has a fixed I2C address, and from what I know about I2C, you cannot have two devices with the same address on the same SDA/SCL pins!" Are you out of luck? You would be, if you didn't have this ultra-cool TCA9548A 1-to-8 I2C multiplexer! Finally, a way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
  Adafruit TB6612 DC and Stepper Motor Driver: Spin two DC motors, step one bi-polar or uni-polar stepper, or fire off two solenoids with 1.2A per channel using the TB6612. These are perhaps better known as "the drivers in our assembled Adafruit Motorshield or Motor HAT." We really like these dual H-bridges, so if you want to control motors without a shield or HAT these are easy to include on any solderless breadboard or perma-proto.
  TVS Diode: A standard TVS diode
  Adafruit DS3231: The datasheet for the DS3231 explains that this part is an "Extremely Accurate I²C-Integrated RTC/TCXO/Crystal". And, hey, it does exactly what it says on the tin! This Real Time Clock (RTC) is the most precise you can get in a small, low power package. Most RTCs use an external 32kHz timing crystal that is used to keep time with low current draw. And that's all well and good, but those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
  SPI Non-Volatile FRAM 8KB: With our SPI FRAM breakout board you can add some FRAM storage to your next DIY project. FRAM allows for a lower power usage and a faster write performance. It's excellent for low-power or inconsistent-power datalogging or data buffering where you want to stream data fast while also keeping the data when there's no power. Unlike Flash or EEPROM there's no pages to worry about. Each byte can be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
  TXB0104 4-channel Bi-Directional Level Shifter: Because the Arduino (and Basic Stamp) are 5V devices, and most modern sensors, displays, flash cards and modes are 3.3V-only, many makers find that they need to perform level shifting/conversion to protect the 3.3V device from 5V. Although one can use resistors to make a divider, for high speed transfers, the resistors can add a lot of slew and cause havoc that is tough to debug. For that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
  Arduino Nano Every: The Nano Every is Arduino’s 5V compatible board in the smallest available form factor: 45x18mm! The Arduino Nano is the preferred board for many projects requiring a small and easy to use microcontroller board. The small footprint and low price, make the Nano Every particularly suited for wearable inventions, low cost robotics, electronic musical instruments, and general use to control smaller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
